# Fritzing sketch EB5222d (saved by Fritzing 0.9.2b)
circuit board: 10.775cm x 6.67568cm
breadboards: 1

parts:
  Eleman1 = Arduino Pro Mini v13
  R1 = Resistor [tolerance=±5% resistance=220 package=THT]
  Eleman2 = RFID-RC522-v2  # not connected
  Nokia_5110_LCD_Module1 = Nokia5110LCDModule  # not connected
  4x4_Keypad = male pin header, 8 pins [form="♂ (male)"]
  RC522 = male pin header, 8 pins [form="♂ (male)"]
  LCD_5110 = male pin header, 8 pins [form="♂ (male)"]
  Q1 = NPN-Transistor [package="TO92 [THT]"]
  R10 = Resistor [tolerance=±5% resistance=220 package=THT]
  SPKR1 = Loudspeaker  # not connected
  LED1 = LED - 5mm [color="Red (633nm)" package="5 mm [THT]"]  # not connected
  Keypad4x1 = Keypad Membran 4x4
  3v3_Input = male pin header, 2 pins [form="♂ (male)"]
  5V_Input = male pin header, 2 pins [form="♂ (male)"]
  LED_G = male pin header, 2 pins [form="♂ (male)"]
  Buzzer = male pin header, 2 pins [form="♂ (male)"]
  LED_R = male pin header, 2 pins [form="♂ (male)"]
  R11 = Resistor [tolerance=±5% resistance=220 package=THT]
  Q2 = NPN-Transistor [package="TO92 [THT]"]
  Q3 = NPN-Transistor [package="TO92 [THT]"]
  LED2 = LED - 5mm [color="Green (555nm)" package="5 mm [THT]"]  # not connected
  R12 = Resistor [tolerance=±5% resistance=220 package=THT]
  R13 = Resistor [tolerance=±5% resistance=220 package=THT]
  R14 = Resistor [tolerance=±5% resistance=220 package=THT]
  U1 = PCF8574 [package="DIP16 [THT]"]

nets:
  GND: Eleman1.GND, RC522.pin6, LCD_5110.pin2, Q1.E, 5V_Input.pin1, Q2.E, Q3.E, U1.GND
  N1: Eleman1.A5, U1.SDA
  N2: Eleman1.RAW, LCD_5110.pin8, 5V_Input.pin2, R12.Pin_1, R13.Pin_1, R14.Pin_1, U1.VCC
  N3: Eleman1.A3, U1.SCL
  N4: Eleman1.D13/SCK, RC522.pin2, LCD_5110.pin7
  N5: Eleman1.D12/MISO, RC522.pin4
  N6: Eleman1.D11_PWM/MOSI, RC522.pin3, LCD_5110.pin6
  N7: Eleman1.D10_PWM/SS, RC522.pin1
  N8: Eleman1.D9_PWM, RC522.pin7
  N9: Eleman1.D8, R11.Pin_1
  N10: Eleman1.D7, R10.Pin_1
  N11: Eleman1.D6_PWM, R1.Pin_1
  N12: Eleman1.D5_PWM, LCD_5110.pin5
  N13: Eleman1.D4, LCD_5110.pin3
  N14: Eleman1.D3_PWM, LCD_5110.pin4
  N15: R1.Pin_0, Q1.B
  N16: 4x4_Keypad.pin1, U1.P0
  N17: 4x4_Keypad.pin2, U1.P1
  N18: 4x4_Keypad.pin3, U1.P2
  N19: 4x4_Keypad.pin4, U1.P3
  N20: 4x4_Keypad.pin5, U1.P4
  N21: 4x4_Keypad.pin6, U1.P5
  N22: 4x4_Keypad.pin7, U1.P6
  N23: 4x4_Keypad.pin8, U1.P7
  N24: RC522.pin8, LCD_5110.pin1, 3v3_Input.pin1
  N25: Q1.C, Buzzer.pin1
  N26: R10.Pin_0, Q2.B
  N27: Keypad4x1.Pin1, Keypad4x1.Pin2, Keypad4x1.Pin3, Keypad4x1.Pin4, Keypad4x1.Pin6, Keypad4x1.Pin7, Keypad4x1.Pin8
  N28: LED_G.pin1, Q2.C
  N29: LED_G.pin2, R12.Pin_0
  N30: Buzzer.pin2, R14.Pin_0
  N31: LED_R.pin1, Q3.C
  N32: LED_R.pin2, R13.Pin_0
  N33: R11.Pin_0, Q3.B

custom parts:
  RFID-RC522-v2: A simple China made RFID-RC522 Reader; do check the pin labels, as this is a MFRC522 based clone.
  : Nokia 5110 LCD with 8 pin. It's a 45mm*45mm module part. Description: The Nokia 5110 is a basic graphic LCD screen for lots of applications. It was originally intended for as a cell phone screen. This one is mounted on an easy to solder PCB. It uses the PCD8544 controller. The PCD8544 is a low power CMOS LCD controller/driver, designed to drive a graphic display of 48 rows and 84 columns. All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
  Keypad Membran 4x4: Membrane Keypad 4x4 Matrix

// code stored in the sketch: AddSetCredit.ino
/**
 * ----------------------------------------------------------------------------
 * This is a MFRC522 library example; see https://github.com/miguelbalboa/rfid
 * for further details and other examples.
 * 
 * NOTE: The library file MFRC522.h has a lot of useful info. Please read it.
 * 
 * Released into the public domain.
 * ----------------------------------------------------------------------------
 * This sample shows how to read and write data blocks on a MIFARE Classic PICC
 * (= card/tag).
 * 
 * BEWARE: Data will be written to the PICC, in sector #1 (blocks #4 to #7).
 * 
 * 
 * Typical pin layout used:
 * -----------------------------------------------------------------------------------------
 *             MFRC522      Arduino       Arduino   Arduino    Arduino          Arduino
 *             Reader/PCD   Uno           Mega      Nano v3    Leonardo/Micro   Pro Micro
 * Signal      Pin          Pin           Pin       Pin        Pin              Pin
 * -----------------------------------------------------------------------------------------
 * RST/Reset   RST          9             5         D9         RESET/ICSP-5     RST
 * SPI SS      SDA(SS)       10            53        D10        10               10
 * SPI MOSI    MOSI         11 / ICSP-4   51        D11        ICSP-4           16
 * SPI MISO    MISO         12 / ICSP-1   50        D12        ICSP-1           14
 * SPI SCK     SCK          13 / ICSP-3   52        D13        ICSP-3           15
 * 
 */

#include <SPI.h>
#include <MFRC522.h>
#include <Adafruit_GFX.h>
#include <Adafruit_PCD8544.h>
#include <Wire.h>
#include <i2ckeypad.h>
#include <Time.h>
#include <DS1307RTC.h>
#include <EEPROM.h>

i2ckeypad kpd = i2ckeypad(0x20, 4, 4);//ROWS, COLS

//Adafruit_PCD8544 display = Adafruit_PCD8544(3, 4, 5, 7, 8);
Adafruit_PCD8544 display = Adafruit_PCD8544(5, 4, 3);

//#define RST_PIN         9           // Configurable, see typical pin layout above
//#define SS_PIN          10          // Configurable, see typical pin layout above
MFRC522 mfrc522(10, 9);   // Create MFRC522 instance.

//MFRC522::MIFARE_Key keyOrg;
MFRC522::MIFARE_Key key;
//MFRC522::MIFARE_Key keyB;

int amount = 0;
char* islem = "Goster";
short islemNo = 0;
short sonislem = -1;

bool fail = 0;

int yearNum;
int monthNum;
int dayNum;
int hourNum;
int minuteNum;
int secondNum;

byte zamanAlani = 1;

/**
 * Initialize.
 */
void setup() {
    pinMode(6,OUTPUT);
    pinMode(7,OUTPUT);
    pinMode(8,OUTPUT);
    
    Serial.begin(9600); // Initialize serial communications with the PC    
    //while (!Serial);    // Do nothing if no serial port is opened (added for Arduinos based on ATMEGA32U4)

    Wire.begin();

    kpd.init();
    
    display.begin();
    // init done
  
    // you can change the contrast around to adapt the display
    // for the best viewing!
    display.setContrast(EEPROM.read(1023));
    digitalWrite(2,HIGH);  
    display.clearDisplay();   // clears the screen and buffer
    
    SPI.begin();        // Init SPI bus
    mfrc522.PCD_Init(); // Init MFRC522 card

    // Prepare the key (used both as key A and as key B)
    key.keyByte[0] = 0xE0;
    key.keyByte[1] = 0xE2;
    key.keyByte[2] = 0xE4;
    key.keyByte[3] = 0xE6;
    key.keyByte[4] = 0xE8;
    key.keyByte[5] = 0xE9;    

//    keyB.keyByte[0] = 0xD0;
//    keyB.keyByte[1] = 0xD2;
//    keyB.keyByte[2] = 0xD4;
//    keyB.keyByte[3] = 0xD6;
//    keyB.keyByte[4] = 0xD8;
//    keyB.keyByte[5] = 0xD9;    
}

void printScr(char* msg, int sz, int x, int y)
{
   // text display
    display.setTextSize(sz);
    display.setTextColor(BLACK);
    display.setCursor(x,y);
    display.println(msg);
}

//void print2digits(int number) {
//  if (number >= 0 && number < 10) {
//    Serial.write('0');
//  }
//  Serial.print(number);
//}

void okBeep(){
              digitalWrite(7,HIGH);
              tone(6,2000,500);     
              delay(500);
              digitalWrite(7,LOW);
              delay(1500);            
}

void warnBeep(){
      digitalWrite(8,HIGH);
      tone(6,2200,400);     
      delay(400);
      digitalWrite(8,LOW);
      delay(200);
      digitalWrite(8,HIGH);
      tone(6,2200,400);     
      delay(400);
      digitalWrite(8,LOW);            
      delay(1000);
}

void initializeMiFARE()
{    
    // Show some details of the PICC (that is: the tag/card)
//    Serial.print(F("Card UID:"));
    dump_byte_array(mfrc522.uid.uidByte, mfrc522.uid.size);
    Serial.println();
//    Serial.print(F("PICC type: "));
    byte piccType = mfrc522.PICC_GetType(mfrc522.uid.sak);
    Serial.println(mfrc522.PICC_GetTypeName(piccType));

    // Check for compatibility
    if (    piccType != MFRC522::PICC_TYPE_MIFARE_MINI
        &&  piccType != MFRC522::PICC_TYPE_MIFARE_1K
        &&  piccType != MFRC522::PICC_TYPE_MIFARE_4K) {
//        Serial.println(F("This sample only works with MIFARE Classic cards."));
        fail = 1;
        return;
    }
}

/**
 * Main loop.
 */
void loop() {  
    fail = 0;

    char b[21];   //declaring character array
    String str;  //declaring string
    str = String(amount); //converting integer into a string
    str.toCharArray(b,8); //passing the value of the string to the character array

    tmElements_t tm;

    if(islemNo == 0)
    {
      while (!RTC.read(tm)) {
        delay(40);
      }

      display.clearDisplay();
      printScr("Kart", 2, 0, 0);
      printScr(islem,2,0,16);  
      printScr("A:Menu",1,0,32);

      str = (tm.Day < 10 ? "0" : "") + String(tm.Day) +  "." + (tm.Month < 10 ? "0" : "") + String(tm.Month) + " " + (tm.Hour < 10 ? "0" : "") + String(tm.Hour) + ":" + (tm.Minute < 10 ? "0" : "") + String(tm.Minute) + ":" + (tm.Second < 10 ? "0" : "") + String(tm.Second);
      str.toCharArray(b,21);
      printScr(b, 1,0,40);
      
      display.display();
    }
    else if(islemNo == 1) //Kart Açma
    {
      display.clearDisplay();
      printScr("Kart No Gir:", 1, 0, 0);
      printScr(b, 1, 0, 8);
      printScr("#:ac  D:Geri", 1, 0, 32);  
      display.display();
    }
    else if(islemNo == 2) //Kart ?ptal
    {
      display.clearDisplay();
      printScr("Kart No Gir:", 1, 0, 0);
      printScr(b, 1, 0, 8);
      printScr("*:iptal D:Geri",1,0,32);  
      display.display();
    }
    else if(islemNo == 3) //Ana Menü
    {
      display.clearDisplay();
      printScr("D:Geri", 1, 0, 0);
      printScr("*:iptal",1,0,8);  
      printScr("#:ac",1,0,16);
      printScr("A:saat",1,0,24);
      printScr("B:ekran",1,0,32);
      display.display();        
    }
    else if(islemNo == 4) //Saat Ayar?
    {
      display.clearDisplay();
      str = "Yil:" + (zamanAlani == 1 ? (String(amount) + "#") : String(yearNum));
      str.toCharArray(b,21);
      printScr(b, 1, 0, 0);

      str = "Ay:" + (zamanAlani == 2 ? (String(amount) + "#") : String(monthNum));
      str.toCharArray(b,21);
      printScr(b, 1, 0, 8);

      str = "Gun:" + (zamanAlani == 3 ? (String(amount) + "#") : String(dayNum));
      str.toCharArray(b,21);
      printScr(b, 1, 0, 16);

      str = "Saat:" + (zamanAlani == 4 ? (String(amount) + "#") : String(hourNum));
      str.toCharArray(b,21);
      printScr(b, 1, 0, 24);

      str = "Dakika:" + (zamanAlani == 5 ? (String(amount) + "#") : String(minuteNum));
      str.toCharArray(b,21);
      printScr(b, 1, 0, 32);
      
      printScr("#Ayarla D:Geri", 1, 0, 40);
      display.display();        
    }
    else if(islemNo == 5) //Ekran Parlakl?k Ayar?
    {
      display.clearDisplay();
      printScr("Deger Gir", 1, 0, 0);      
      printScr("(0-20):", 1, 0, 8); 
      printScr(b, 1, 0, 16);
      printScr("#:Tamam D:Geri", 1, 0, 32);
      display.display();        
    }
    
    //Keypad.ListenforEventKey();
    char Key = kpd.get_key();
    if(Key != '\0')
    {
      Serial.println(Key);    //printScr("Kart   Okutun", 2, 0, 8);
      switch(Key)
      {
        case '0' :
          amount = amount * 10;
          break;
        case '1' :
          amount = amount * 10 + 1;
          break;
        case '2' :
          amount = amount * 10 + 2;
          break;
        case '3' :
          amount = amount * 10 + 3;
          break;
        case '4' :
          amount = amount * 10 + 4;
          break;
        case '5' :
          amount = amount * 10 + 5;
          break;
        case '6' :
          amount = amount * 10 + 6;
          break;
        case '7' :
          amount = amount * 10 + 7;
          break;
        case '8' :
          amount = amount * 10 + 8;
          break;
        case '9' :
          amount = amount * 10 + 9;
          break;
        case 'A' :
          if(islemNo == 0 || islemNo == 1 || islemNo == 2)
          {
            islem = "Menu";
            islemNo = 3;
          }
          else if(islemNo == 3)
          {
            while (!RTC.read(tm)) {
              delay(40);
            }
            
            yearNum = tmYearToCalendar(tm.Year);
            amount = yearNum;
            monthNum = tm.Month;
            dayNum = tm.Day;
            hourNum = tm.Hour;
            minuteNum = tm.Minute;
            
            islemNo = 4;
          }
          break;
        case 'B' :
          if(islemNo == 3)
          {
            islemNo = 5;
          }
          else
          {
            amount = amount + 1;
          }
          break;
        case 'C' :
          amount = 0;
          break;
        case 'D' :
          islemNo = 0;
          islem = "Goster";
          break;
        case '*' :
          if(islemNo == 3)
          {
            islem = "iptal";
            islemNo = 2;
          }
          else if(islemNo == 2)
          {
            if(amount > 100 && amount < 1000)
            {
              //iptal bilgisini EEPROM'a yaz.
              EEPROM.write(amount,2);
              display.clearDisplay();
              printScr("Kart iptal", 1, 0, 0);
              printScr("Edildi!", 1, 0, 8);
              display.display();                      

              okBeep();
              
              islem = 0;
            }
            else
            {
              display.clearDisplay();
              printScr("Hatali Kart No!!!", 1, 0, 0);
              display.display();          

              warnBeep();
            }
          }
          break;
        case '#' :
          if(islemNo == 5)
          {
            if(amount >= 0 && amount <= 20)
            {
              //açma bilgisini EEPROM'a yaz
              EEPROM.write(1023, amount + 35);
              display.setContrast(EEPROM.read(1023));
              display.clearDisplay();
              printScr("Parlaklik", 1, 0, 0);
              printScr("Ayarlandi", 1, 0, 8);
              String str = String(EEPROM.read(1023));
              str.toCharArray(b,21);
              printScr(b,1,0,16);
              display.display();                      

              okBeep();
            }
            else{
              display.clearDisplay();
              printScr("Yanlis", 1, 0, 0);
              printScr("Deger!!!", 1, 0, 8);
              display.display();                      

              warnBeep();
            }
          }
          else if(islemNo == 4)
          {
            if(zamanAlani == 1){
              yearNum = amount;
              amount = monthNum;
              zamanAlani = 2;
            }
            else if(zamanAlani == 2){
              monthNum = amount;
              amount = dayNum;
              zamanAlani = 3;
            }
            else if(zamanAlani == 3){
              dayNum = amount;
              amount = hourNum;
              zamanAlani = 4;
            }
            else if(zamanAlani == 4){
              hourNum = amount;
              amount = minuteNum;
              zamanAlani = 5;              
            }
            else if(zamanAlani == 5){
              minuteNum = amount;              
              amount = tmYearToCalendar(tm.Year);

              tm.Year = yearNum - 1970;
              tm.Month = monthNum;
              tm.Day = dayNum;
              tm.Hour = hourNum;
              tm.Minute = minuteNum;
              RTC.set(makeTime(tm));
              setTime(hourNum, minuteNum, tm.Second, dayNum, monthNum, yearNum);

              display.clearDisplay();
              printScr("Saat", 1, 0, 0);
              printScr("Ayarlandi", 1, 0, 8);
              
              str = (dayNum < 10 ? "0" : "") + String(dayNum) +  "." + (monthNum < 10 ? "0" : "") + String(monthNum) + " " + (hourNum < 10 ? "0" : "") + String(hourNum) + ":" + (minuteNum < 10 ? "0" : "") + String(minuteNum) + ":" + (tm.Second < 10 ? "0" : "") + String(tm.Second);
              str.toCharArray(b,21);
              printScr(b, 1,0,16);
              
              str = String(yearNum);
              str.toCharArray(b,21);
              printScr(b, 1,0,24);

              display.display();                      

              zamanAlani = 1;
              okBeep();
            }

          }
          else if(islemNo == 3)
          {
            islem = "Ac";
            islemNo = 1;
          }
          else if(islemNo == 1)
          {
            if(amount > 100 && amount < 1000)
            {
              //açma bilgisini EEPROM'a yaz
              EEPROM.write(amount,1);
              display.clearDisplay();
              printScr("Kart Acildi!", 1, 0, 0);
              display.display();                      

              okBeep();
              
              islem = 0;
            }
            else
            {
              display.clearDisplay();
              printScr("Hatali Kart No!!!", 1, 0, 0);
              display.display();                      

              warnBeep();
            }
          }
          break;
      }
    }

    // Look for new cards
    if ( ! mfrc522.PICC_IsNewCardPresent())   
       return;    
    // Select one of the cards
    if ( ! mfrc522.PICC_ReadCardSerial())
       return;

    initializeMiFARE();

    // In this sample we use the second sector,
    // that is: sector #1, covering block #4 up to and including block #7
    byte sector         = 1;
    byte blockAddr      = 4;
    byte dataBlock[]    = {
        0x01, 0x02, 0x03, 0x04, //  1,  2,   3,  4,
        0x05, 0x06, 0x07, 0x08, //  5,  6,   7,  8,
        0x08, 0x09, 0xff, 0x0b, //  9, 10, 255, 12,
        0x0c, 0x0d, 0x0e, 0x0f  // 13, 14,  15, 16
    };

    byte trailerBlock   = 7;
    MFRC522::StatusCode status;
    byte buffer[18];
    byte size = sizeof(buffer);

    // Authenticate using key A
    //Serial.println(F("Authenticating using key A..."));
    status = (MFRC522::StatusCode) mfrc522.PCD_Authenticate(MFRC522::PICC_CMD_MF_AUTH_KEY_A, trailerBlock, &key, &(mfrc522.uid));
    if (status != MFRC522::STATUS_OK) {
        //Serial.print(F("PCD_Authenticate() failed: "));
        Serial.println(mfrc522.GetStatusCodeName(status));
        return;
    }

    // Read data from the block
//    Serial.print(F("Reading data from block ")); Serial.print(blockAddr);
//    Serial.println(F(" ..."));
    status = (MFRC522::StatusCode) mfrc522.MIFARE_Read(blockAddr, buffer, &size);
    if (status != MFRC522::STATUS_OK) {
//        Serial.print(F("MIFARE_Read() failed: "));
//        Serial.println(mfrc522.GetStatusCodeName(status));
                
        fail = 1;
    }
//    Serial.print(F("Data in block ")); Serial.print(blockAddr); Serial.println(F(":"));
    dump_byte_array(buffer, 16); Serial.println();
//    Serial.println();

    unsigned int cardNum = buffer[0];
    cardNum = cardNum * 256 + buffer[1];

    yearNum = buffer[2];
    monthNum = buffer[3];
    dayNum = buffer[4];
    hourNum = buffer[5];
    minuteNum = buffer[6];
    secondNum = buffer[7];

    unsigned long useCount = buffer[8];
    useCount = 256 * useCount + buffer[9];
    useCount = 256 * useCount + buffer[10];
    useCount = 256 * useCount + buffer[11];

//    Serial.print(F("Card Number : "));Serial.print(cardNum);
//    Serial.println();
//    Serial.print("Ok, Last Use Time = ");
//    print2digits(hourNum);
//    Serial.write(':');
//    print2digits(minuteNum);
//    Serial.write(':');
//    print2digits(secondNum);
//    Serial.print(", Date (D/M/Y) = ");
//    Serial.print(dayNum);
//    Serial.write('/');
//    Serial.print(monthNum);
//    Serial.write('/');
//    Serial.print(yearNum);
//    Serial.println();
//    Serial.print(F("Use Count : "));Serial.print(useCount);
//    Serial.println();


    byte cardStatus = EEPROM.read(cardNum);
    if(cardStatus == 2)
    {
//      Serial.print(F("Card Status : "));Serial.print(cardStatus);
//      Serial.println();

          display.clearDisplay();
          printScr("Kart", 2, 0, 0);
          printScr("iptal", 2, 0, 16);
          printScr("Edilmis", 2, 0, 32);
          display.display();

      warnBeep();
      goto End;
    }

    if(!fail) //??lemi s?f?rla
    {
      islemNo = 0;
      islem = "Goster";
      useCount += 1;
      
      if (RTC.read(tm)) {
        
        //Saat'e göre kar??la?t?rma yap?l?yor. Ayn? gün içinde ikinci kez kabul edilmemeli.  
        if(tm.Day != dayNum || tm.Month != monthNum)
        {
          dataBlock[0] = buffer[0];
          dataBlock[1] = buffer[1];
  
          dataBlock[2] = tmYearToCalendar(tm.Year) - 2000; //??lem zaman? yaz?l?yor
          dataBlock[3] = tm.Month;
          dataBlock[4] = tm.Day;
          dataBlock[5] = tm.Hour;
          dataBlock[6] = tm.Minute;
          dataBlock[7] = tm.Second;
  
          dataBlock[8] = (useCount >> 24) & 0xFF; //Kullan?m adedi bilgisi yaz?l?yor.
          dataBlock[9] = (useCount >> 16) & 0xFF;
          dataBlock[10] = (useCount >> 8) & 0xFF;
          dataBlock[11] = useCount & 0xFF;;      
  
          // Write data to the block
          //Serial.print(F("Writing data into block ")); Serial.print(blockAddr);
          //Serial.println(F(" ..."));
          dump_byte_array(dataBlock, 16); Serial.println();
          status = (MFRC522::StatusCode) mfrc522.MIFARE_Write(blockAddr, dataBlock, 16);
          if (status != MFRC522::STATUS_OK) {
              //Serial.print(F("MIFARE_Write() failed: "));
              //Serial.println(mfrc522.GetStatusCodeName(status));
          }
          //Serial.println();
  
          // Read data from the block (again, should now be what we have written)
          //Serial.print(F("Reading data from block ")); Serial.print(blockAddr);
          //Serial.println(F(" ..."));
          status = (MFRC522::StatusCode) mfrc522.MIFARE_Read(blockAddr, buffer, &size);
          if (status != MFRC522::STATUS_OK) {
              Serial.print(F("MIFARE_Read() failed: "));
              Serial.println(mfrc522.GetStatusCodeName(status));
          }
          Serial.print(F("Data in block ")); Serial.print(blockAddr); Serial.println(F(":"));
          dump_byte_array(buffer, 16); Serial.println();
              
          // Check that data in block is what we have written
          // by counting the number of bytes that are equal
          //Serial.println(F("Checking result..."));
          byte count = 0;
          for (byte i = 0; i < 16; i++) {
              // Compare buffer (= what we've read) with dataBlock (= what we've written)
              if (buffer[i] == dataBlock[i])
                  count++;
          }
           
          //Serial.println(cardNum, DEC);
          //Serial.print(F("Number of bytes that match = ")); Serial.println(count);
          if (count == 16) {
              Serial.println(F("Success :-)"));
  
              display.clearDisplay();
              printScr("Kart No", 2, 0, 0);
  
              str = String(cardNum); //converting integer into a string
              str.toCharArray(b,8); //passing the value of the string to the character array
              // text display
              printScr(b,2,0,16);
  
              str = String("S:") + String(useCount); //converting integer into a string
              str.toCharArray(b,8); //passing the value of the string to the character array
              // text display
              str.toCharArray(b,8);
              printScr(b, 2, 0, 32);
              display.display();
  
              okBeep();
          } else {
//              Serial.println(F("Failure, no match :-("));
//              Serial.println(F("  perhaps the write didn't work properly..."));
          }
          Serial.println();
              
          // Dump the sector data
//          Serial.println(F("Current data in sector:"));
          mfrc522.PICC_DumpMifareClassicSectorToSerial(&(mfrc522.uid), &key, sector);
          Serial.println();
        }
        else
        {
          display.clearDisplay();
          printScr("Bugun", 2, 0, 0);
          printScr("Okunmus", 2, 0, 16);
          str = "Kart" + String(cardNum);
          str.toCharArray(b,21);
          printScr(b, 2, 0, 32);
          display.display();
          warnBeep();
        }
      } 
      else 
      {
        if (RTC.chipPresent()) {
//          Serial.println("The DS1307 is stopped.  Please run the SetTime");
//          Serial.println("example to initialize the time and begin running.");
          Serial.println();
        } else {
//          Serial.println("DS1307 read error!  Please check the circuitry.");
          Serial.println();
        }
      }
    }
    else
    {
        islem = "Hata!!!";
        digitalWrite(8,HIGH);
        tone(6,1800,400);
        delay(400);
        digitalWrite(8,LOW);
        delay(200);
        digitalWrite(8,HIGH);
        tone(6,1800,400);
        delay(400);
        digitalWrite(8,LOW);
        delay(200);
        digitalWrite(8,HIGH);
        tone(6,1800,400);      
        delay(400);
        digitalWrite(8,LOW);
    }
End:    
    // Halt PICC
    mfrc522.PICC_HaltA();
    // Stop encryption on PCD
    mfrc522.PCD_StopCrypto1();    

}

/**
 * Helper routine to dump a byte array as hex values to Serial.
 */
void dump_byte_array(byte *buffer, byte bufferSize) {
    for (byte i = 0; i < bufferSize; i++) {
        Serial.print(buffer[i] < 0x10 ? " 0" : " ");
        Serial.print(buffer[i], HEX);
    }
}
