# Fritzing sketch RFID_PIN_Zugangskontrolle (saved by Fritzing 0.9.3b)
breadboards: 1

parts:
  LCD1 = LCD screen
  J1 = Piezo Speaker
  Keypad4x2 = Keypad Membran 4x4
  Eleman3 = RFID-RC522-v2
  Bauteil1 = Arduino Uno (Rev3)
  R1 = Resistor [tolerance=±5% resistance=220 package=THT]
  LED1 = LED - 5mm [color="Red (633nm)" package="5 mm [THT]"]
  LED2 = LED - 5mm [color="Green (565nm)" package="5 mm [THT]"]
  R2 = Resistor [tolerance=±5% resistance=220 package=THT]
  R3 = Resistor [tolerance=±5% resistance=220 package=THT]

nets:
  N1: LCD1.DB6, Bauteil1.5V
  GND: LCD1.DB7, J1.pin1, Eleman3.GND, Bauteil1.GND, R2.Pin_0, R3.Pin_0
  N2: LCD1.LED+, Bauteil1.A5/SCL
  N3: LCD1.LED-, Bauteil1.A4/SDA
  N4: J1.pin2, R1.Pin_1
  N5: Keypad4x2.Pin1, Bauteil1.D5_PWM
  N6: Keypad4x2.Pin2, Bauteil1.D4
  N7: Keypad4x2.Pin3, Bauteil1.D3_PWM
  N8: Keypad4x2.Pin4, Bauteil1.D2
  N9: Keypad4x2.Pin5, Bauteil1.D8
  N10: Keypad4x2.Pin6, Bauteil1.D7
  N11: Keypad4x2.Pin7, Bauteil1.D6_PWM
  N12: Eleman3.SDA, Bauteil1.D10_PWM/SS
  N13: Eleman3.SCK, Bauteil1.D13/SCK
  N14: Eleman3.MOSI, Bauteil1.D11_PWM/MOSI
  N15: Eleman3.MISO, Bauteil1.D12/MISO
  N16: Eleman3.RST, Bauteil1.A2
  3.3V: Eleman3.3.3V, Bauteil1.3V3
  N17: Bauteil1.A0, LED1.anode
  N18: Bauteil1.A1, LED2.anode
  N19: Bauteil1.D9_PWM, R1.Pin_0
  N20: LED1.cathode, R3.Pin_1
  N21: LED2.cathode, R2.Pin_1

custom parts:
  Keypad Membran 4x4: Membrane Keypad 4x4 Matrix
  RFID-RC522-v2: A simple China made RFID-RC522 Reader; do check the pin labels, as this is a MFRC522 based clone.
